# Fritzing sketch BerryGPS Fritzing Schematic + PCB (saved by Fritzing 0.9.3b)
circuit board: 1.66984cm x 4.30397cm
breadboards: 1

parts:
  BerryGPS_-_IMU_Portion = Adafruit LSM9DS1 9DoF Breakout [part_number="Adafruit #3387"]
  STM32 = STM32F103C8T6 blue mini board
  BerryGPS_-_GPS_Portion = u-blox NEO-6M GPS Breakout

nets:
  N1: BerryGPS_-_IMU_Portion.SDA, STM32.B11
  N2: BerryGPS_-_IMU_Portion.SCL, STM32.B10
  GND: BerryGPS_-_IMU_Portion.GND, STM32.G, STM32.GND, BerryGPS_-_GPS_Portion.GND
  VIN: BerryGPS_-_IMU_Portion.VIN, STM32.3.3V, STM32.3.3
  N3: STM32.B12, BerryGPS_-_GPS_Portion.VCC
  N4: STM32.A9, BerryGPS_-_GPS_Portion.TXD
  N5: STM32.A10, BerryGPS_-_GPS_Portion.RXD

notes:
  Kevin Lieng

custom parts:
  Adafruit LSM9DS1 9DoF Breakout: Add motion, direction and orientation sensing to your Arduino project with this all-in-one 9-DOF sensor. Inside the chip are three sensors, one is a classic 3-axis accelerometer, which can tell you which direction is down towards the Earth (by measuring gravity) or how fast the board is accelerating in 3D space. The other is a 3-axis magnetometer that can sense where the strongest magnetic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
