# Fritzing sketch Feather +BerryIMU  Remake PCB (saved by Fritzing 0.9.3b)
circuit board: 8cm x 7.5cm
breadboards: 1

parts:
  Feather_ESP8266 = Adafruit Feather 32u4 Basic Proto [part_number="Adafruit #2771"]
  BerryGPS-IMU = double row male pin header, 8 pins [form="♂ (male)"]

nets:
  N1: Feather_ESP8266.GND, BerryGPS-IMU.pin7
  N2: Feather_ESP8266.+3V3, BerryGPS-IMU.pin1
  N3: Feather_ESP8266.3, BerryGPS-IMU.pin3
  N4: Feather_ESP8266.2, BerryGPS-IMU.pin2

notes:
  3.3V
  5V
  SDA
  SCL
  GND
  GPS_RX
  GPS_TX
  Kevin Lieng

custom parts:
  Adafruit Feather 32u4 Basic Proto: At the Feather 32u4's heart is at ATmega32u4 clocked at 8 MHz and at 3.3V logic, a chip setup we've had tons of experience with as it's the same as the Flora. This chip has 32K of flash and 2K of RAM, with built in USB so not only does it have a USB-to-Serial program & debug capability built in with no need for an FTDI-like chip, it can also act like a mouse, keyboard, USB MIDI device, etc.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
