# Fritzing sketch NoSTM32 (saved by Fritzing 0.9.3b)
circuit board: 5.88802cm x 3.14979cm
breadboards: 1

parts:
  BerryGPS = double row male pin header, 8 pins [form="♂ (male)"]
  STM32 = double row male pin header, 8 pins [form="♂ (male)"]

nets:
  N1: BerryGPS.pin1, STM32.pin8
  N2: BerryGPS.pin2, STM32.pin7
  N3: BerryGPS.pin3, STM32.pin6
  N4: BerryGPS.pin5, STM32.pin4
  N5: BerryGPS.pin6, STM32.pin3
  N6: BerryGPS.pin7, STM32.pin2
  N7: BerryGPS.pin8, STM32.pin1

notes:
  3.3V
  5V
  SDA
  SCL
  GND
  GPS_RX
  GPS_TX
  Kevin Lieng
